# Fritzing sketch dcf77 (saved by Fritzing 0.9.2b)
circuit board: 7.7cm x 5.7cm
circuit board: 7.7cm x 5.7cm
breadboards: 3

parts:
  OLED1 = 128x64 Monochrom OLED Display with SPI Control
  GPS1 = Adafruit Ultimate GPS Breakout
  U2 = 74HC04_HEX_INVERTER [package=dil14]
  J1 = AVR ISP 6 Pin [package=2x3_lock]
  R1 = Resistor [tolerance=±5% resistance=1k package=THT]
  Q1_BC337 = NPN-Transistor [package="TO92 [THT]"]
  XTAL1 = CRYSTAL - kHz [frequency="16 Mhz"]
  L1 = Inductor [inductance=8.2mH package="400 mil [THT]"]
  C2 = Ceramic Capacitor [capacitance=22pF package="100 mil [THT, multilayer]"]
  C3 = Ceramic Capacitor [capacitance=22pF package="100 mil [THT, multilayer]"]
  R3 = Resistor [tolerance=±5% resistance=10k package=THT]
  R4 = Resistor [tolerance=±5% resistance=100k package=THT]
  C4 = Ceramic Capacitor [capacitance=47pF package="100 mil [THT, multilayer]"]
  C5 = Ceramic Capacitor [capacitance=47pF package="100 mil [THT, multilayer]"]
  R7 = Resistor [tolerance=±5% resistance=100k package=THT]
  R8 = Resistor [tolerance=±5% resistance=220 package=THT]
  XTAL2_77_5Khz = CRYSTAL - kHz
  R13 = Resistor [tolerance=±5% resistance=100k package=THT]
  R6 = Resistor [tolerance=±5% resistance=470k package=THT]
  R5 = Resistor [tolerance=±5% resistance=4.7M package=THT]
  S4 = Square Pushbutton
  S5 = Square Pushbutton
  U3 = IC, DIP package, 16 pins [chip_label=ds3231]
  BAT2 = Battery Holders [package=battery-aa-kit]
  Q2_BC337 = NPN-Transistor [package="TO92 [THT]"]
  R18 = Resistor [tolerance=±5% resistance=1k package=THT]
  R19 = Resistor [tolerance=±5% resistance=1k package=THT]
  IC2 = IC, DIP package, 6 pins [chip_label=LTC4054-4.2]
  IC3 = IC, DIP package, 8 pins [chip_label=LT1302]
  LED1 = LED - 3mm [color="Red (633nm)" package="3 mm [THT]"]
  R20 = Resistor [tolerance=±5% resistance=220 package=THT]
  R21 = Resistor [tolerance=±5% resistance=1.5k package=THT]
  L2 = Inductor [inductance=220µH package="400 mil [THT]"]
  R22 = Resistor [tolerance=±5% resistance=22k package=THT]
  C14 = Ceramic Capacitor [capacitance=10nF package="100 mil [THT, multilayer]"]
  R23 = Resistor [tolerance=±5% resistance=100k package=THT]
  R24 = Resistor [tolerance=±5% resistance=100k package=THT]
  D1 = Schottky Diode [part_number=1N5817 package="300 mil [THT]"]
  R25 = Resistor [tolerance=±5% resistance=1M package=THT]
  R26 = Resistor [tolerance=±5% resistance=100k package=THT]
  R27 = Resistor [tolerance=±5% resistance=100k package=THT]
  R29 = Resistor [tolerance=±5% resistance=1M package=THT]
  R30 = Resistor [tolerance=±5% resistance=100k package=THT]
  J2 = Screw terminal - 2 pins [package=THT]
  JACK1 = 2.1mm DC Barrel Jack
  C17 = Electrolytic Capacitor [capacitance=100µF voltage=35V package="100 mil [THT, electrolytic]"]
  C18 = Electrolytic Capacitor [capacitance=330µF voltage=35V package="100 mil [THT, electrolytic]"]
  C12 = Electrolytic Capacitor [capacitance=1000μF voltage=35V package="100 mil [THT, electrolytic]"]
  C15 = Electrolytic Capacitor [capacitance=10µF voltage=35V package="100 mil [THT, electrolytic]"]
  C16 = Tantalum Capacitor [capacitance=220µF voltage=35V package="200 mil [THT, tantalum]"]
  R31 = Resistor [tolerance=±5% resistance=100k package=THT]
  R32 = Resistor [tolerance=±5% resistance=100k package=THT]
  R33 = Resistor [tolerance=±5% resistance=100k package=THT]
  U4 = Mini-USB _B_ connector with 5th pin broken out. [package=usb-minib]
  C11 = Electrolytic Capacitor [capacitance=1µF voltage=35V package="100 mil [THT, electrolytic]"]
  C1 = Ceramic Capacitor [capacitance=510pF package="100 mil [THT, multilayer]"]
  U5 = Voltage Regulator - 5V [package="TO220 [THT]"]
  R28 = Trimmer Potentiometer [maximum_resistance=500kΩ package=THT]
  C13 = Electrolytic Capacitor [capacitance=1µF voltage=35V package="200 mil [THT, electrolytic]"]
  J3 = screw terminal, 2 pins
  S6 = Square Pushbutton
  D2 = SOLAR-IXYS [package=solarbit-12x1]
  U1 = atmega328 [package=dip]
  BAT1 = Battery Holders [package=battcom_20mm_pth]
  C6 = Ceramic Capacitor [capacitance=510pF package="200 mil [THT, multilayer]"]

nets:
  N1: OLED1.Data, J1.4, U1.D11_(PWM)
  N2: OLED1.Clock, J1.3, U1.D13
  N3: OLED1.SA0/DC, U1.D9_(PWM)
  N4: OLED1.Reset, J1.1, U1.D12
  N5: OLED1.CS, U1.D10_(PWM)
  3V3: OLED1.3v3, GPS1.3.3V, J1.2, R3.Pin_0, R4.Pin_0, R13.Pin_0, U3.pin2, BAT2.+, IC2.pin3, IC3.pin6, L2.pin_1, R29.Pin_1, C17.+, C18.+, C16.+, R31.Pin_0, R32.Pin_0, R33.Pin_1, C13.+, J3.pin2, D2.A, U1.VCC, U1.AVCC
  GND: OLED1.GND, GPS1.GND, U2.GND, J1.6, Q1_BC337.E, L1.pin_0, C2.0, C3.1, C4.1, C5.0, S4.leg1, S5.leg1, U3.pin5, U3.pin6, U3.pin7, U3.pin8, U3.pin9, U3.pin10, U3.pin11, U3.pin12, U3.pin13, BAT2.-, IC2.pin2, IC2.pin5, IC3.pin1, IC3.pin8, R21.Pin_1, C14.1, R24.Pin_0, R26.Pin_0, R30.Pin_0, J2.pin1, JACK1.center, C17.-, C18.-, C12.-, C15.-, C16.-, U4.D-, C11.-, C1.0, U5.GND, C13.-, J3.pin1, S6.leg1, D2.C, U1.GND, BAT1.-, C6.0
  N6: GPS1.VBAT, U3.pin14, BAT1.+
  N7: GPS1.TX, U1.D0_(RX)
  N8: GPS1.RX, U1.D1_(TX)
  N9: GPS1.PPS, U1.D2
  N10: U2.1A, C5.1, XTAL2_77_5Khz.pin_0, R5.Pin_1
  N11: U2.1Y, U2.2A, R6.Pin_0, R5.Pin_0
  N12: U2.2Y, U2.5A
  N13: U2.5Y, R18.Pin_0
  N14: U2.VCC, Q2_BC337.C, D1.cathode, R25.Pin_1, C15.+, R28.leg2
  N15: J1.5, R3.Pin_1, S6.leg0, U1.RESET
  N16: R1.Pin_0, L1.pin_1, R8.Pin_1, J2.pin2, C1.1
  N17: R1.Pin_1, R19.Pin_1, C6.1
  N18: Q1_BC337.B, R7.Pin_0
  N19: Q1_BC337.C, R8.Pin_0
  N20: XTAL1.pin_0, C3.0, U1.XLAT2
  N21: XTAL1.pin_1, C2.1, U1.XLAT1
  N22: R4.Pin_1, S4.leg0, U1.D8
  N23: C4.0, XTAL2_77_5Khz.pin_1, R6.Pin_1
  N24: R7.Pin_1, U1.D5_(PWM)
  N25: R13.Pin_1, S5.leg0, U1.D7
  N26: U3.pin3, R33.Pin_0, U1.D3_(PWM)
  N27: U3.pin15, R32.Pin_1, U1.A5
  N28: U3.pin16, R31.Pin_1, U1.A4
  N29: Q2_BC337.E, R19.Pin_0
  N30: Q2_BC337.B, R18.Pin_1
  N31: IC2.pin1, R20.Pin_0
  N32: IC2.pin4, LED1.anode, U4.ID, C11.+, U5.output_voltage
  N33: IC2.pin6, R21.Pin_0
  N34: IC3.pin2, R22.Pin_1
  N35: IC3.pin3, R23.Pin_0
  N36: IC3.pin4, R26.Pin_1, R27.Pin_1
  N37: IC3.pin7, L2.pin_0, D1.anode
  N38: LED1.cathode, R20.Pin_1
  N39: R22.Pin_0, C14.0
  N40: R23.Pin_1, U1.D6_(PWM)
  N41: R24.Pin_1, R25.Pin_0, U1.A3
  N42: R27.Pin_0, R28.leg1, R28.wiper
  N43: R29.Pin_0, R30.Pin_1, U1.A0
  N44: JACK1.switch, JACK1.sleeve, C12.+, U5.input_voltage

custom parts:
  CRYSTAL - kHz: Crystal oscillator, used in watches and other timing applications, typically 32.768KHZ
  2.1mm DC Barrel Jack: 2.1mm DC Barrel Jack with Thru-Hole Connectors (breadboardable)
