# Fritzing sketch dcf77_simple (saved by Fritzing 0.9.2b)
circuit board: 7.5cm x 12cm
breadboards: 2

parts:
  OLED1 = 128x64 Monochrom OLED Display with SPI Control
  U1 = atmega328 [package=dip]
  GPS1 = Adafruit Ultimate GPS Breakout
  LED1 = LED - 5mm [color="Red (633nm)" package="5 mm [THT]"]
  U2 = 74HC04_HEX_INVERTER [package=dil14]
  J1 = AVR ISP 6 Pin [package=2x3_lock]
  R1 = Resistor [tolerance=±5% resistance=4.7k package=THT]
  Q1_BC337 = NPN-Transistor [package="TO92 [THT]"]
  XTAL1 = CRYSTAL - kHz [frequency="16 Mhz"]
  L1 = Inductor [inductance=8.2mH package="400 mil [THT]"]
  C2 = Ceramic Capacitor [capacitance=22pF package="100 mil [THT, multilayer]"]
  C3 = Ceramic Capacitor [capacitance=22pF package="100 mil [THT, multilayer]"]
  R3 = Resistor [tolerance=±5% resistance=10k package=THT]
  R4 = Resistor [tolerance=±5% resistance=10k package=THT]
  C4 = Ceramic Capacitor [capacitance=47pF package="100 mil [THT, multilayer]"]
  C5 = Ceramic Capacitor [capacitance=47pF package="100 mil [THT, multilayer]"]
  R7 = Resistor [tolerance=±5% resistance=100k package=THT]
  R8 = Resistor [tolerance=±5% resistance=1k package=THT]
  BAT1 = Battery Holders [package=battcom_20mm_pth]
  XTAL2_77_5Khz = CRYSTAL - kHz
  R13 = Resistor [tolerance=±5% resistance=10k package=THT]
  R6 = Resistor [tolerance=±5% resistance=470k package=THT]
  R5 = Resistor [tolerance=±5% resistance=4.7M package=THT]
  C1 = Ceramic Capacitor [capacitance=510pF package="200 mil [THT, multilayer]"]
  R16 = Resistor [tolerance=±5% resistance=220 package=THT]
  LED2 = LED - 5mm [color="Red (633nm)" package="5 mm [THT]"]
  R17 = Resistor [tolerance=±5% resistance=100 package=THT]
  power_supply = Breadboard Power Supply Board SMD
  S4 = Square Pushbutton
  S5 = Square Pushbutton
  S6 = Square Pushbutton
  U3 = IC, DIP package, 16 pins [chip_label=ds3231]
  BAT2 = Battery Holders [package=battery-aa-kit]

nets:
  N1: OLED1.Data, U1.D11_(PWM), J1.4
  N2: OLED1.Clock, U1.D13, J1.3
  N3: OLED1.SA0/DC, U1.D9_(PWM)
  N4: OLED1.Reset, U1.D12, J1.1
  N5: OLED1.CS, U1.D10_(PWM)
  VCC: OLED1.Vin, U1.VCC, U1.AVCC, U1.AREF, GPS1.VIN, U2.VCC, J1.2, R3.Pin_0, R4.Pin_0, R13.Pin_0, power_supply.VCC, U3.pin2
  GND: OLED1.GND, U1.GND, GPS1.GND, U2.GND, J1.6, Q1_BC337.E, L1.pin_0, C2.0, C3.1, C4.1, C5.0, BAT1.-, C1.0, R16.Pin_0, R17.Pin_1, power_supply.GND, S4.leg1, S5.leg1, S6.leg1, U3.pin5, U3.pin7, U3.pin8, U3.pin9, U3.pin13, BAT2.-
  N6: U1.RESET, J1.5, R3.Pin_1, S6.leg0
  N7: U1.D0_(RX), GPS1.TX
  N8: U1.D1_(TX), GPS1.RX
  N9: U1.D2, GPS1.PPS
  N10: U1.D3_(PWM), U3.pin3
  N11: U1.D4, R4.Pin_1, S4.leg0
  N12: U1.XLAT1, XTAL1.pin_1, C2.1
  N13: U1.XLAT2, XTAL1.pin_0, C3.0
  N14: U1.D5_(PWM), LED1.anode, R7.Pin_1
  N15: U1.D7, R13.Pin_1, S5.leg0
  N16: U1.D8, GPS1.EN, LED2.anode
  N17: U1.A4, U3.pin16
  N18: U1.A5, U3.pin15
  N19: GPS1.VBAT, BAT1.+, U3.pin14
  N20: LED1.cathode, R16.Pin_1
  N21: U2.1A, C5.1, XTAL2_77_5Khz.pin_0, R5.Pin_1
  N22: U2.1Y, U2.2A, R6.Pin_0, R5.Pin_0
  N23: U2.2Y, U2.5A
  N24: U2.5Y, R1.Pin_1
  N25: R1.Pin_0, L1.pin_1, R8.Pin_1, C1.1
  N26: Q1_BC337.B, R7.Pin_0
  N27: Q1_BC337.C, R8.Pin_0
  N28: C4.0, XTAL2_77_5Khz.pin_1, R6.Pin_1
  N29: LED2.cathode, R17.Pin_0
  N30: power_supply.VIN, BAT2.+

custom parts:
  CRYSTAL - kHz: Crystal oscillator, used in watches and other timing applications, typically 32.768KHZ
