# Fritzing sketch dcf77_v22 (saved by Fritzing 0.9.2b)
circuit board: 14cm x 7.00001cm
stripboards: 2

parts:
  J1 = AVR ISP 6 Pin [package=2x3_lock]
  77_5 = CRYSTAL - kHz
  BAT1 = Battery Holders [package=battcom_20mm_pth]
  IC3 = SO08 [chip_label=AD8532ARZ package=SO]
  U2_DS3231 = SO16 [chip_label=ds3231 package=SO]
  R6 = Resistor [tolerance=±5% resistance=100 package="0805 [SMD]"]
  C10 = Ceramic Capacitor [capacitance=47pF package="0805 [SMD, multilayer]"]
  C11 = Ceramic Capacitor [capacitance=47pF package="0805 [SMD, multilayer]"]
  R14 = Resistor [tolerance=±5% resistance=100 package="0805 [SMD]"]
  R13 = Resistor [tolerance=±5% resistance=4.7M package="0805 [SMD]"]
  C4 = Ceramic Capacitor [capacitance=560pF voltage=16V package="0805 [SMD, multilayer]"]
  C3 = Ceramic Capacitor [capacitance=560pF voltage=16V package="0805 [SMD, multilayer]"]
  C6 = Ceramic Capacitor [capacitance=2.20nF voltage=16V package="0805 [SMD, multilayer]"]
  C0 = Ceramic Capacitor [capacitance=2.20nF voltage=16V package="0805 [SMD, multilayer]"]
  R5 = Resistor [tolerance=±1% resistance=1k package="0805 [SMD]"]
  R10 = Resistor [tolerance=±5% resistance=100 package="0805 [SMD]"]
  C9 = Ceramic Capacitor [capacitance=22pF package="0805 [SMD, multilayer]"]
  C8 = Ceramic Capacitor [capacitance=22pF package="0805 [SMD, multilayer]"]
  R4 = Resistor [tolerance=±5% resistance=100k package="0805 [SMD]"]
  R19 = Resistor [tolerance=±5% resistance=100k package="0805 [SMD]"]
  R18 = Resistor [tolerance=±5% resistance=100k package="0805 [SMD]"]
  R26 = Resistor [tolerance=±1% resistance=1M package="0805 [SMD]"]
  R27 = Resistor [tolerance=±1% resistance=100k package="0805 [SMD]"]
  R3 = Resistor [tolerance=±5% resistance=100k package="0805 [SMD]"]
  R8 = Resistor [tolerance=±5% resistance=1k package="0805 [SMD]"]
  C2 = Tantalum Capacitor [capacitance=47µF voltage=35V package="B 3528 [SMD, tantalum]"]
  C5 = Tantalum Capacitor [capacitance=47µF voltage=35V package="B 3528 [SMD, tantalum]"]
  Q2 = NPN-Transistor [part_number=" BC847" package="SOT-23 [SMD]"]
  JP2 = Header 2 [package=molex-1x2_lock]
  JP1 = Header 4 [package=molex-1x4_lock]
  IC1 = FGPMMOPA6C [package=MTK3339]
  U4A328 = ATmega328 [package=tqfp]
  U5_4069 = SOIC-14 [chip_label=4069 package=SO]
  JACK1 = 2.1mm DC Barrel Jack
  U4 = USB Connectors [package=usb-microb]
  ENCODER1 = Rotary Encoder with Knob
  R8_2 = Resistor [tolerance=±5% resistance=1k package="0805 [SMD]"]
  JP4 = Header 2 [package=molex-1x2_lock]
  R1 = Resistor [tolerance=±5% resistance=220 package="0805 [SMD]"]
  R12 = Resistor [tolerance=±5% resistance=100k package="0805 [SMD]"]
  C12 = Electrolytic Capacitor [capacitance=1000μF voltage=35V package="100 mil [THT, electrolytic]"]
  C13 = Electrolytic Capacitor [capacitance=1µF voltage=35V package="100 mil [THT, electrolytic]"]
  R11 = Resistor [tolerance=±5% resistance=100k package="0805 [SMD]"]
  R16 = Resistor [tolerance=±5% resistance=1M package="0805 [SMD]"]
  LED1 = smd LED [color="Red (633nm)" package="1206 [SMD]"]
  IC3_(alt) = SO08 [chip_label=AD8531ARZ package=SO]
  R22 = Resistor [tolerance=±1% resistance=1M package="0805 [SMD]"]
  LED2 = smd LED [color="Red (633nm)" package="1206 [SMD]"]
  R7 = Resistor [tolerance=±5% resistance=100k package="0805 [SMD]"]
  R17 = Resistor [tolerance=±5% resistance=220 package="0805 [SMD]"]
  R23 = Resistor [tolerance=±1% resistance=100k package="0805 [SMD]"]
  JP6 = Header 4 [package=molex-1x4_lock]
  JP5 = Header 3 [package=molex-1x3_lock]
  C7 = Tantalum Capacitor [capacitance=100µF voltage=35V package="B 3528 [SMD, tantalum]"]
  JP7 = Header 6 [package=molex-1x6_lock]
  R2 = Resistor [tolerance=±5% resistance=100k package="0805 [SMD]"]
  R9 = Resistor [tolerance=±5% resistance=100k package="0805 [SMD]"]
  U6 = Voltage Regulator - Variable [package="TO220 [THT]"]
  Q3 = MOSFET-NCHANNEL [package=dpak]
  U7 = LTC4054-4.2 [package=sot23-5]
  R30 = Resistor [tolerance=±5% resistance=1.5k package="0805 [SMD]"]
  C1 = Ceramic Capacitor [capacitance=750pF voltage=0.1kV package="100 mil [THT, multilayer]"]
  R15 = Resistor [tolerance=±5% resistance=1k package="0805 [SMD]"]
  Q1 = NPN-Transistor [part_number=" BC847" package="SOT-23 [SMD]"]
  R20 = Resistor [tolerance=±5% resistance=100k package="0805 [SMD]"]
  S3 = Pushbutton [package="[THT]"]
  R31 = Resistor [tolerance=±1% resistance=0 package="0805 [SMD]"]
  U8 = INA-139 [package=sot23-5]
  R29 = Resistor [tolerance=±1% resistance=0 package="1206 [SMD]"]
  R28 = Resistor [tolerance=±1% resistance=4.7M package="0805 [SMD]"]
  C14 = Tantalum Capacitor [capacitance=220µF voltage=35V package="B 3528 [SMD, tantalum]"]
  XTAL1 = Crystal [frequency="8 MHz" package=THT]

nets:
  OLED RESET: J1.1, U4A328.PB4(MISO), JP5.2
  GPS V+/OLED V+: J1.2, IC3.8, U2_DS3231.2, R4.Pin_0, R19.Pin_0, R18.Pin_0, R26.Pin_1, R3.Pin_1, IC1.Vcc, U4A328.VCC, U4A328.AVCC, U5_4069.14, IC3_(alt).7, JP6.2, C7.+, JP7.6, R2.Pin_0, R9.Pin_0, R20.Pin_0, U8.VIN-, R29.Pin_1, C14.+
  OLED Clock: J1.3, U4A328.PB5(SCK), JP5.3
  OLED DATA: J1.4, U4A328.PB3(MOSI_OC2), JP5.1
  N1: J1.5, U2_DS3231.4, U4A328.PC6(_RESET), R9.Pin_1, S3.Pin_2
  BAT1-/GND/GPS GND/L1 (5.9 mH) GND/OLED GND/Solar-: J1.6, BAT1.-, U2_DS3231.5, U2_DS3231.6, U2_DS3231.7, U2_DS3231.8, U2_DS3231.9, U2_DS3231.10, U2_DS3231.11, U2_DS3231.12, U2_DS3231.13, C9.1, C8.0, R27.Pin_0, JP2.2, JP1.4, IC1.NC, IC1.GND, U4A328.GND, U4A328.AGND, JACK1.center, U4.GND, ENCODER1.no_name_yet#3, ENCODER1.no_name_yet#4, JP4.1, R1.Pin_1, C12.-, C13.-, R16.Pin_1, R23.Pin_0, JP6.1, C7.-, JP7.5, U6.ADJ, Q3.S, U7.GND, R30.Pin_1, C1.0, S3.Pin_3, S3.Pin_4, U8.GND, R28.Pin_0, C14.-
  N2: 77_5.pin_0, C10.1, R13.Pin_1, U5_4069.1
  N3: 77_5.pin_1, C11.0, R14.Pin_1
  GPS Vbat: BAT1.+, U2_DS3231.14, IC1.Vbackup, JP7.4
  N4: IC3.1, IC3.2, C0.1, C2.+, IC3_(alt).2, IC3_(alt).6
  N5: IC3.3, C3.0, R5.Pin_1, IC3_(alt).3
  N6: IC3.4, C10.0, C11.1, C4.1, C3.1, Q2.2, U5_4069.7, IC3_(alt).4, Q3.D, Q1.2, R31.Pin_0
  N7: IC3.5, C4.0, R8_2.Pin_0
  N8: IC3.6, IC3.7, C6.0, C5.+
  N9: U2_DS3231.3, R3.Pin_0, U4A328.PD3(INT1)
  N10: U2_DS3231.15, U4A328.PC5(ADC5_SCL), R2.Pin_1
  N11: U2_DS3231.16, R4.Pin_1, U4A328.PC4(ADC4_SDA)
  N12: R6.Pin_0, Q1.1
  N13: R6.Pin_1, C0.0, R5.Pin_0, R8.Pin_1
  N14: R14.Pin_0, R13.Pin_0, U5_4069.2, U5_4069.3
  N15: C6.1, R10.Pin_1, R8_2.Pin_1, R15.Pin_0
  N16: R10.Pin_0, Q2.1
  N17: C9.0, U4A328.PB7(XTAL2_TOSC2), XTAL1.pin_0
  N18: C8.1, U4A328.PB6(XTAL1_TOSC1), XTAL1.pin_1
  N19: R19.Pin_1, U4A328.PD7(AIN1), ENCODER1.no_name_yet#2
  N20: R18.Pin_1, U4A328.PB0(ICP), ENCODER1.no_name_yet#5
  N21: R26.Pin_0, R27.Pin_1, U4A328.PC0(ADC0)
  N22: R8.Pin_0, U5_4069.12
  L2 25 SIG: C2.-, JP1.1
  L2 25 GND: C5.-, JP1.2, R31.Pin_1
  N23: Q2.0, R11.Pin_0
  BAT1+/Solar+: JP2.1, JP4.2, U7.BAT, U8.VIN+, U8.V+, R29.Pin_0
  L1 (5.9 mH) SIG: JP1.3, C1.1
  N24: IC1.3D-FIX, LED1.anode
  GPS PPS: IC1.1PPS, U4A328.PD2(INT0), JP7.3
  GPS TX: IC1.TX, U4A328.PD0(RXD), JP7.2
  GPS RX: IC1.RX, U4A328.PD1(TXD), JP7.1
  N25: U4A328.PD4(XCK_T0), R12.Pin_0
  N26: U4A328.PD5(T1), R11.Pin_1, R7.Pin_1
  N27: U4A328.PD6(AIN0), ENCODER1.no_name_yet#1, R20.Pin_1
  OLED DC: U4A328.PB1(OC1A), JP6.3
  OLED CS: U4A328.PB2(SS_OC1B), JP6.4
  N28: U4A328.PC1(ADC1), U8.OUT, R28.Pin_1
  N29: U4A328.PC2(ADC2), R22.Pin_0, R23.Pin_1
  N30: U5_4069.4, U5_4069.5
  N31: U5_4069.6, U5_4069.11, U5_4069.13
  N32: U5_4069.8, R15.Pin_1
  N33: U5_4069.9, U5_4069.10
  N34: JACK1.switch, JACK1.sleeve, C12.+, U6.IN
  N35: U4.VBUS, C13.+, R22.Pin_1, LED2.anode, U6.OUT, U7.PROG
  N36: R1.Pin_0, LED1.cathode
  N37: R12.Pin_1, R16.Pin_0, Q3.G
  N38: LED2.cathode, R17.Pin_1
  N39: R7.Pin_0, Q1.0
  N40: R17.Pin_0, U7.CHRG
  N41: U7.Vcc, R30.Pin_0

custom parts:
  CRYSTAL - kHz: Crystal oscillator, used in watches and other timing applications, typically 32.768KHZ
  FGPMMOPA6C: FGPMMOPA6C GPS Standalone Module
  2.1mm DC Barrel Jack: 2.1mm DC Barrel Jack with Thru-Hole Connectors (breadboardable)
  Rotary Encoder with Knob: Rotary Encoder with 1/4" Shaft and Knob
  LTC4054-4.2: Standalone Linear Li-Ion Battery Charger with Thermal Regulation in ThinSOT
  INA-139: INA1x9 High-Side Measurement Current Shunt Monitor
